// Logisim project NANDs_MUX_8.1.circ as structural Verilog: 1 circuit, main circuit main
module main (
  input  in_1,
  input  in_2,
  input  in_3,
  input  in_4,
  input  in_5,
  input  in_6,
  input  in_7,
  input  in_8,
  input  [2:0] in_9
);

  wire button_1_out, button_2_out, button_3_out, button_4_out, multiplexer_1_out, nand_1_out, nand_2_out,
       nand_3_out;

  Button button_1 (.out(button_1_out));
  Button button_2 (.out(button_2_out));
  Button button_3 (.out(button_3_out));
  Button button_4 (.out(button_4_out));
  nand nand_1 (nand_1_out, button_1_out, button_2_out);
  nand nand_2 (nand_2_out, button_3_out, button_4_out);
  Multiplexer #(.select(3)) multiplexer_1 (
    .in0(in_3), .in1(in_2), .in2(in_1), .in3(in_4), .in4(in_5), .in5(in_6), .in6(in_7), .in7(in_8),
    .out(multiplexer_1_out), .sel(in_9));
  LED led_1 (.in(multiplexer_1_out));
  nand nand_3 (nand_3_out, nand_1_out, nand_2_out);
  LED led_2 (.in(nand_3_out));
endmodule
