// Logisim project BCD.circ as structural Verilog: 1 circuit, main circuit main
module main (
  input  [7:0] in_1,
  output [7:0] out_2,
  output [3:0] BLOQUE_1,
  output [3:0] UNIDADES,
  output [7:0] out_5
);

  wire adder_1_cout, adder_2_cout, adder_3_cout, adder_4_cout, adder_5_cout, adder_6_cout, adder_7_cout,
       adder_8_cout, adder_9_cout, adder_9_out, adder_10_cout, adder_10_out, adder_11_cout, adder_11_out,
       adder_12_cout, adder_12_out, adder_13_cout, adder_14_cout, adder_15_cout, adder_16_cout,
       adder_17_cout, adder_17_out, adder_18_cout, adder_18_out, adder_19_cout, adder_19_out, adder_20_cout,
       adder_20_out, adder_21_cout, adder_22_cout, adder_23_cout, adder_24_cout, adder_25_cout, adder_25_out,
       adder_26_cout, adder_26_out, adder_27_cout, adder_27_out, adder_28_cout, adder_28_out, adder_29_cout,
       adder_30_cout, adder_31_cout, adder_32_cout, adder_33_cout, adder_33_out, adder_34_cout, adder_34_out,
       adder_35_cout, adder_35_out, adder_36_cout, adder_36_out, adder_37_cout, adder_38_cout, adder_39_cout,
       adder_40_cout, adder_41_cout, adder_41_out, adder_42_cout, adder_42_out, adder_43_cout, adder_43_out,
       adder_44_cout, adder_44_out, adder_45_cout, adder_46_cout, adder_47_cout, adder_48_cout,
       adder_49_cout, adder_49_out, adder_50_cout, adder_50_out, adder_51_cout, adder_51_out, adder_52_cout,
       adder_52_out, adder_53_cout, adder_54_cout, adder_55_cout, adder_56_cout, adder_57_cout, adder_57_out,
       adder_58_cout, adder_58_out, adder_59_cout, adder_59_out, adder_60_cout, adder_60_out, adder_61_cout,
       adder_62_cout, adder_63_cout, adder_64_cout, adder_65_cout, adder_65_out, adder_66_cout, adder_66_out,
       adder_67_cout, adder_67_out, adder_68_cout, adder_68_out, adder_69_cout, adder_70_cout, adder_71_cout,
       adder_72_cout, adder_73_cout, adder_73_out, adder_74_cout, adder_74_out, adder_75_cout, adder_75_out,
       adder_76_cout, adder_76_out, undriven_5, undriven_6, undriven_7, undriven_8;
  wire [7:0] adder_1_out, adder_2_out, adder_3_out, adder_4_out, adder_5_out, adder_6_out, adder_7_out,
       adder_8_out, adder_13_out, adder_14_out, adder_15_out, adder_16_out, adder_21_out, adder_22_out,
       adder_23_out, adder_24_out, adder_29_out, adder_30_out, adder_31_out, adder_32_out, adder_37_out,
       adder_38_out, adder_39_out, adder_40_out, adder_45_out, adder_46_out, adder_47_out, adder_48_out,
       adder_53_out, adder_54_out, adder_55_out, adder_56_out, adder_61_out, adder_63_out, adder_64_out,
       adder_69_out, adder_71_out, adder_72_out, undriven, undriven_3, undriven_4, undriven_9, undriven_10,
       undriven_11, undriven_12, undriven_13, undriven_14;
  wire [7:4] undriven_2;

  Adder adder_1 (.a(undriven), .b(undriven), .out(adder_1_out), .cin(1'b0), .cout(adder_1_cout));
  Adder adder_2 (
    .a({undriven_2, in_1[7:4]}), .b({undriven_2, in_1[7:4]}), .out(adder_2_out), .cin(adder_1_cout),
    .cout(adder_2_cout));
  Adder adder_3 (.a(undriven_4), .b(undriven_3), .out(adder_3_out), .cin(adder_2_cout), .cout(adder_3_cout));
  Adder adder_4 (.a(undriven_4), .b(undriven_4), .out(adder_4_out), .cin(adder_3_cout), .cout(adder_4_cout));
  Adder adder_5 (.a(adder_1_out), .b(undriven), .out(adder_5_out), .cin(1'b0), .cout(adder_5_cout));
  Adder adder_6 (
    .a(adder_2_out), .b({undriven_2, in_1[7:4]}), .out(adder_6_out), .cin(adder_5_cout), .cout(adder_6_cout));
  Adder adder_7 (.a(adder_3_out), .b(undriven_3), .out(adder_7_out), .cin(adder_6_cout), .cout(adder_7_cout));
  Adder adder_8 (.a(adder_4_out), .b(undriven_4), .out(adder_8_out), .cin(adder_7_cout), .cout(adder_8_cout));
  Adder #(.width(1)) adder_9 (.a(adder_4_cout), .b(1'b0), .out(adder_9_out), .cin(adder_8_cout), .cout(adder_9_cout));
  Adder #(.width(1)) adder_10 (.a(1'b0), .b(1'b0), .out(adder_10_out), .cin(adder_9_cout), .cout(adder_10_cout));
  Adder #(.width(1)) adder_11 (.a(1'b0), .b(1'b0), .out(adder_11_out), .cin(adder_10_cout), .cout(adder_11_cout));
  Adder #(.width(1)) adder_12 (.a(1'b0), .b(1'b0), .out(adder_12_out), .cin(adder_11_cout), .cout(adder_12_cout));
  LED led_1 (.in(adder_12_cout));
  Adder adder_13 (.a(adder_5_out), .b(undriven), .out(adder_13_out), .cin(1'b0), .cout(adder_13_cout));
  Adder adder_14 (
    .a(adder_6_out), .b({undriven_2, in_1[7:4]}), .out(adder_14_out), .cin(adder_13_cout),
    .cout(adder_14_cout));
  Adder adder_15 (.a(adder_7_out), .b(undriven_3), .out(adder_15_out), .cin(adder_14_cout), .cout(adder_15_cout));
  Adder adder_16 (.a(adder_8_out), .b(undriven_4), .out(adder_16_out), .cin(adder_15_cout), .cout(adder_16_cout));
  Adder #(.width(1)) adder_17 (
    .a(adder_9_out), .b(1'b0), .out(adder_17_out), .cin(adder_16_cout), .cout(adder_17_cout));
  Adder #(.width(1)) adder_18 (
    .a(adder_10_out), .b(1'b0), .out(adder_18_out), .cin(adder_17_cout), .cout(adder_18_cout));
  Adder #(.width(1)) adder_19 (
    .a(adder_11_out), .b(1'b0), .out(adder_19_out), .cin(adder_18_cout), .cout(adder_19_cout));
  Adder #(.width(1)) adder_20 (
    .a(adder_12_out), .b(1'b0), .out(adder_20_out), .cin(adder_19_cout), .cout(adder_20_cout));
  LED led_2 (.in(adder_20_cout));
  Adder adder_21 (.a(adder_13_out), .b(undriven), .out(adder_21_out), .cin(1'b0), .cout(adder_21_cout));
  Adder adder_22 (
    .a(adder_14_out), .b({undriven_2, in_1[7:4]}), .out(adder_22_out), .cin(adder_21_cout),
    .cout(adder_22_cout));
  Adder adder_23 (.a(adder_15_out), .b(undriven_3), .out(adder_23_out), .cin(adder_22_cout), .cout(adder_23_cout));
  Adder adder_24 (.a(adder_16_out), .b(undriven_4), .out(adder_24_out), .cin(adder_23_cout), .cout(adder_24_cout));
  Adder #(.width(1)) adder_25 (
    .a(adder_17_out), .b(1'b0), .out(adder_25_out), .cin(adder_24_cout), .cout(adder_25_cout));
  Adder #(.width(1)) adder_26 (
    .a(adder_18_out), .b(1'b0), .out(adder_26_out), .cin(adder_25_cout), .cout(adder_26_cout));
  Adder #(.width(1)) adder_27 (
    .a(adder_19_out), .b(1'b0), .out(adder_27_out), .cin(adder_26_cout), .cout(adder_27_cout));
  Adder #(.width(1)) adder_28 (
    .a(adder_20_out), .b(1'b0), .out(adder_28_out), .cin(adder_27_cout), .cout(adder_28_cout));
  LED led_3 (.in(adder_28_cout));
  Adder adder_29 (.a(adder_21_out), .b(undriven), .out(adder_29_out), .cin(1'b0), .cout(adder_29_cout));
  Adder adder_30 (
    .a(adder_22_out), .b({undriven_2, in_1[7:4]}), .out(adder_30_out), .cin(adder_29_cout),
    .cout(adder_30_cout));
  Adder adder_31 (.a(adder_23_out), .b(undriven_3), .out(adder_31_out), .cin(adder_30_cout), .cout(adder_31_cout));
  Adder adder_32 (.a(adder_24_out), .b(undriven_4), .out(adder_32_out), .cin(adder_31_cout), .cout(adder_32_cout));
  Adder #(.width(1)) adder_33 (
    .a(adder_25_out), .b(1'b0), .out(adder_33_out), .cin(adder_32_cout), .cout(adder_33_cout));
  Adder #(.width(1)) adder_34 (
    .a(adder_26_out), .b(1'b0), .out(adder_34_out), .cin(adder_33_cout), .cout(adder_34_cout));
  Adder #(.width(1)) adder_35 (
    .a(adder_27_out), .b(1'b0), .out(adder_35_out), .cin(adder_34_cout), .cout(adder_35_cout));
  Adder #(.width(1)) adder_36 (
    .a(adder_28_out), .b(1'b0), .out(adder_36_out), .cin(adder_35_cout), .cout(adder_36_cout));
  LED led_4 (.in(adder_36_cout));
  Adder adder_37 (.a(adder_29_out), .b(undriven), .out(adder_37_out), .cin(1'b0), .cout(adder_37_cout));
  Adder adder_38 (
    .a(adder_30_out), .b({undriven_2, in_1[7:4]}), .out(adder_38_out), .cin(adder_37_cout),
    .cout(adder_38_cout));
  Adder adder_39 (.a(adder_31_out), .b(undriven_3), .out(adder_39_out), .cin(adder_38_cout), .cout(adder_39_cout));
  Adder adder_40 (.a(adder_32_out), .b(undriven_4), .out(adder_40_out), .cin(adder_39_cout), .cout(adder_40_cout));
  Adder #(.width(1)) adder_41 (
    .a(adder_33_out), .b(1'b0), .out(adder_41_out), .cin(adder_40_cout), .cout(adder_41_cout));
  Adder #(.width(1)) adder_42 (
    .a(adder_34_out), .b(1'b0), .out(adder_42_out), .cin(adder_41_cout), .cout(adder_42_cout));
  Adder #(.width(1)) adder_43 (
    .a(adder_35_out), .b(1'b0), .out(adder_43_out), .cin(adder_42_cout), .cout(adder_43_cout));
  Adder #(.width(1)) adder_44 (
    .a(adder_36_out), .b(1'b0), .out(adder_44_out), .cin(adder_43_cout), .cout(adder_44_cout));
  LED led_5 (.in(adder_44_cout));
  Adder adder_45 (.a(adder_37_out), .b(undriven), .out(adder_45_out), .cin(1'b0), .cout(adder_45_cout));
  Adder adder_46 (
    .a(adder_38_out), .b({undriven_2, in_1[7:4]}), .out(adder_46_out), .cin(adder_45_cout),
    .cout(adder_46_cout));
  Adder adder_47 (.a(adder_39_out), .b(undriven_3), .out(adder_47_out), .cin(adder_46_cout), .cout(adder_47_cout));
  Adder adder_48 (.a(adder_40_out), .b(undriven_4), .out(adder_48_out), .cin(adder_47_cout), .cout(adder_48_cout));
  Adder #(.width(1)) adder_49 (
    .a(adder_41_out), .b(1'b0), .out(adder_49_out), .cin(adder_48_cout), .cout(adder_49_cout));
  Adder #(.width(1)) adder_50 (
    .a(adder_42_out), .b(1'b0), .out(adder_50_out), .cin(adder_49_cout), .cout(adder_50_cout));
  Adder #(.width(1)) adder_51 (
    .a(adder_43_out), .b(1'b0), .out(adder_51_out), .cin(adder_50_cout), .cout(adder_51_cout));
  Adder #(.width(1)) adder_52 (
    .a(adder_44_out), .b(1'b0), .out(adder_52_out), .cin(adder_51_cout), .cout(adder_52_cout));
  LED led_6 (.in(adder_52_cout));
  Adder adder_53 (.a(adder_45_out), .b(undriven), .out(adder_53_out), .cin(1'b0), .cout(adder_53_cout));
  Adder adder_54 (
    .a(adder_46_out), .b({undriven_2, in_1[7:4]}), .out(adder_54_out), .cin(adder_53_cout),
    .cout(adder_54_cout));
  Adder adder_55 (.a(adder_47_out), .b(undriven_3), .out(adder_55_out), .cin(adder_54_cout), .cout(adder_55_cout));
  Adder adder_56 (.a(adder_48_out), .b(undriven_4), .out(adder_56_out), .cin(adder_55_cout), .cout(adder_56_cout));
  Adder #(.width(1)) adder_57 (
    .a(adder_49_out), .b(1'b0), .out(adder_57_out), .cin(adder_56_cout), .cout(adder_57_cout));
  Adder #(.width(1)) adder_58 (
    .a(adder_50_out), .b(1'b0), .out(adder_58_out), .cin(adder_57_cout), .cout(adder_58_cout));
  Adder #(.width(1)) adder_59 (
    .a(adder_51_out), .b(1'b0), .out(adder_59_out), .cin(adder_58_cout), .cout(adder_59_cout));
  Adder #(.width(1)) adder_60 (
    .a(adder_52_out), .b(1'b0), .out(adder_60_out), .cin(adder_59_cout), .cout(adder_60_cout));
  LED led_7 (.in(adder_60_cout));
  Adder adder_61 (.a(adder_53_out), .b(undriven), .out(adder_61_out), .cin(1'b0), .cout(adder_61_cout));
  Adder adder_62 (
    .a(adder_54_out), .b({undriven_2, in_1[7:4]}), .out(out_5), .cin(adder_61_cout), .cout(adder_62_cout));
  Adder adder_63 (.a(adder_55_out), .b(undriven_3), .out(adder_63_out), .cin(adder_62_cout), .cout(adder_63_cout));
  Adder adder_64 (.a(adder_56_out), .b(undriven_4), .out(adder_64_out), .cin(adder_63_cout), .cout(adder_64_cout));
  Adder #(.width(1)) adder_65 (
    .a(adder_57_out), .b(1'b0), .out(adder_65_out), .cin(adder_64_cout), .cout(adder_65_cout));
  Adder #(.width(1)) adder_66 (
    .a(adder_58_out), .b(1'b0), .out(adder_66_out), .cin(adder_65_cout), .cout(adder_66_cout));
  Adder #(.width(1)) adder_67 (
    .a(adder_59_out), .b(1'b0), .out(adder_67_out), .cin(adder_66_cout), .cout(adder_67_cout));
  Adder #(.width(1)) adder_68 (
    .a(adder_60_out), .b(1'b0), .out(adder_68_out), .cin(adder_67_cout), .cout(adder_68_cout));
  LED led_8 (.in(adder_68_cout));
  Adder adder_69 (.a(undriven_11), .b(undriven_14), .out(adder_69_out), .cin(1'b0), .cout(adder_69_cout));
  Adder #(.width(4)) adder_70 (
    .a(out_5[3:0]), .b(in_1[3:0]), .out(out_2[3:0]), .cin(adder_69_cout), .cout(adder_70_cout));
  Adder adder_71 (.a(undriven_10), .b(undriven_13), .out(adder_71_out), .cin(adder_70_cout), .cout(adder_71_cout));
  Adder adder_72 (.a(undriven_9), .b(undriven_12), .out(adder_72_out), .cin(adder_71_cout), .cout(adder_72_cout));
  Adder #(.width(1)) adder_73 (.a(undriven_8), .b(1'b0), .out(adder_73_out), .cin(adder_72_cout), .cout(adder_73_cout));
  Adder #(.width(1)) adder_74 (.a(undriven_7), .b(1'b0), .out(adder_74_out), .cin(adder_73_cout), .cout(adder_74_cout));
  Adder #(.width(1)) adder_75 (.a(undriven_6), .b(1'b0), .out(adder_75_out), .cin(adder_74_cout), .cout(adder_75_cout));
  Adder #(.width(1)) adder_76 (.a(undriven_5), .b(1'b0), .out(adder_76_out), .cin(adder_75_cout), .cout(adder_76_cout));
  LED led_9 (.in(adder_76_cout));
  // Pins of 4 and 8 bits meet at out_5
  // Pins of 4 and 8 bits meet at out_2
  // Pins of 4 and 8 bits meet at {undriven_2, in_1[7:4]}

  assign BLOQUE_1 = in_1[7:4];
  assign UNIDADES = in_1[3:0];

  // Notes on the sheet:
  //   ENTRADA NUMERO BCD DIGITOS - 8 BITS
  //   DECENAS
  //   BLOQUE 2
  //   SALIDA
  //   VALOR BINARIO
  //   2 DIGITOS - 8 BITS
  //   MULTIPLICADOR DECENAS
  //   SE SUMA 10 VECES EL NUMERO BINARIO DEL BLOQUE1
  //   SUMADOR FINAL
  //   DECENAS + UNIDADES
  //   BLOQUE 1*10 + BLOQUE 2
endmodule
